// Logisim project branch-comp.circ as structural Verilog: 1 circuit, main circuit branch_comp
module branch_comp (
  input  [31:0] BrData1,
  input  [31:0] BrData2,
  input  BrUn,
  output BrEq,
  output BrLt
);

  wire is_equal0, is_equal1, is_less0, is_less1;

  Comparator #(.width(32)) comparator_1 (.a(BrData1), .b(BrData2), .eq(is_equal0), .lt(is_less0));  // open: gt
  Comparator #(.mode("unsigned"), .width(32)) comparator_2 (
    .a(BrData1), .b(BrData2), .eq(is_equal1), .lt(is_less1));  // open: gt
  Multiplexer #(.enable("false")) multiplexer_1 (.in0(is_equal0), .in1(is_equal1), .out(BrEq), .sel(BrUn));
  Multiplexer #(.enable("false")) multiplexer_2 (.in0(is_less0), .in1(is_less1), .out(BrLt), .sel(BrUn));

  // Notes on the sheet:
  //   INPUTS to your circuit
  //   DON'T CHANGE THE LOCATIONS OF THE INPUTS AND OUTPUTS!
  //   OUTPUT from your circuit
endmodule
