// Logisim project control-logic.circ as structural Verilog: 1 circuit, main circuit control_logic
module control_logic (
  input  [31:0] Instruction,
  input  BrEq,
  input  BrLt,
  output PCSel,
  output RegWEn,
  output [2:0] ImmSel,
  output BrUn,
  output ASel,
  output BSel,
  output [3:0] ALUSel,
  output MemWEn,
  output [1:0] WBSel
);

  wire add, addi, and_1_out, and_8_out, and_9_out, and_13_out, andd, andi, auipc, beq, bge, bgeu, blt, bltu,
       bne, comparator_1_eq, comparator_2_eq, comparator_3_eq, comparator_4_eq, comparator_5_eq,
       comparator_6_eq, comparator_7_eq, comparator_8_eq, comparator_9_eq, comparator_10_eq,
       comparator_11_eq, comparator_12_eq, comparator_13_eq, comparator_14_eq, comparator_15_eq,
       comparator_16_eq, comparator_17_eq, comparator_18_eq, comparator_19_eq, comparator_20_eq,
       comparator_21_eq, comparator_22_eq, comparator_23_eq, comparator_24_eq, comparator_25_eq,
       comparator_26_eq, comparator_27_eq, comparator_28_eq, comparator_29_eq, comparator_30_eq,
       comparator_31_eq, comparator_32_eq, comparator_33_eq, comparator_34_eq, comparator_35_eq,
       comparator_36_eq, comparator_37_eq, comparator_38_eq, comparator_39_eq, comparator_40_eq,
       comparator_41_eq, comparator_42_eq, comparator_43_eq, comparator_44_eq, comparator_45_eq,
       comparator_46_eq, comparator_47_eq, comparator_48_eq, comparator_49_eq, comparator_50_eq,
       comparator_51_eq, comparator_52_eq, comparator_53_eq, comparator_54_eq, comparator_55_eq, InputSel,
       is_beq, is_bge, is_bgeu, is_blt, is_bltu, is_bne, jal, jalr, lb, lh, lui, lw, mul, mulh, mulhu,
       not_1_out, not_2_out, not_3_out, ori, orr, sb, sh, slli, slll, slt, slti, sraa, srai, srli, srll, sub,
       sw, xori, xorr;
  wire [1:0] RomInput2;
  wire [4:0] RomInput1;
  wire [5:0] multiplexer_1_out;
  wire [15:14] rom_1_data;

  Comparator #(.width(7)) comparator_1 (.a(Instruction[6:0]), .b(7'b0010011), .eq(comparator_1_eq));  // open: gt, lt
  Comparator #(.width(3)) comparator_2 (.a(Instruction[14:12]), .b(3'b000), .eq(comparator_2_eq));  // open: gt, lt
  Comparator #(.width(3)) comparator_3 (.a(Instruction[14:12]), .b(3'b001), .eq(comparator_3_eq));  // open: gt, lt
  Comparator #(.width(3)) comparator_4 (.a(Instruction[14:12]), .b(3'b010), .eq(comparator_4_eq));  // open: gt, lt
  Comparator #(.width(3)) comparator_5 (.a(Instruction[14:12]), .b(3'b100), .eq(comparator_5_eq));  // open: gt, lt
  Comparator #(.width(3)) comparator_6 (.a(Instruction[14:12]), .b(3'b101), .eq(comparator_6_eq));  // open: gt, lt
  Comparator #(.width(3)) comparator_7 (.a(Instruction[14:12]), .b(3'b110), .eq(comparator_7_eq));  // open: gt, lt
  Comparator #(.width(3)) comparator_8 (.a(Instruction[14:12]), .b(3'b111), .eq(comparator_8_eq));  // open: gt, lt
  Multiplexer #(.enable("false"), .width(6)) multiplexer_1 (
    .in0({1'b0, RomInput1}), .in1({4'b1000, RomInput2}), .out(multiplexer_1_out), .sel(InputSel));
  and and_1 (and_1_out, comparator_1_eq, comparator_6_eq);
  Comparator #(.width(7)) comparator_9 (.a(Instruction[31:25]), .b(7'b0100000), .eq(comparator_9_eq));  // open: gt, lt
  ROM #(.addrWidth(6), .dataWidth(16)) rom_1 (
    .addr(multiplexer_1_out), .data({rom_1_data, WBSel, MemWEn, ALUSel, BSel, ASel, BrUn, ImmSel, RegWEn}));
  Demultiplexer #(.enable("false")) demultiplexer_1 (.out0(srli), .out1(srai), .in(and_1_out), .sel(comparator_9_eq));
  and and_2 (addi, comparator_1_eq, comparator_2_eq);
  and and_3 (slli, comparator_1_eq, comparator_3_eq);
  and and_4 (slti, comparator_1_eq, comparator_4_eq);
  and and_5 (xori, comparator_1_eq, comparator_5_eq);
  and and_6 (ori, comparator_1_eq, comparator_7_eq);
  and and_7 (andi, comparator_1_eq, comparator_8_eq);
  Comparator #(.width(7)) comparator_10 (.a(Instruction[6:0]), .b(7'b0110011), .eq(comparator_10_eq));  // open: gt, lt
  Comparator #(.width(3)) comparator_11 (.a(Instruction[14:12]), .b(3'b000), .eq(comparator_11_eq));  // open: gt, lt
  Comparator #(.width(7)) comparator_12 (.a(Instruction[31:25]), .b({7{1'b0}}), .eq(comparator_12_eq));  // open: gt, lt
  Comparator #(.width(7)) comparator_13 (
    .a(Instruction[31:25]), .b(7'b0000001), .eq(comparator_13_eq));  // open: gt, lt
  Comparator #(.width(7)) comparator_14 (
    .a(Instruction[31:25]), .b(7'b0100000), .eq(comparator_14_eq));  // open: gt, lt
  Comparator #(.width(3)) comparator_15 (.a(Instruction[14:12]), .b(3'b001), .eq(comparator_15_eq));  // open: gt, lt
  Comparator #(.width(7)) comparator_16 (
    .a(Instruction[31:25]), .b(7'b0000001), .eq(comparator_16_eq));  // open: gt, lt
  Comparator #(.width(3)) comparator_17 (.a(Instruction[14:12]), .b(3'b011), .eq(comparator_17_eq));  // open: gt, lt
  Comparator #(.width(3)) comparator_18 (.a(Instruction[14:12]), .b(3'b010), .eq(comparator_18_eq));  // open: gt, lt
  Comparator #(.width(3)) comparator_19 (.a(Instruction[14:12]), .b(3'b100), .eq(comparator_19_eq));  // open: gt, lt
  Comparator #(.width(3)) comparator_20 (.a(Instruction[14:12]), .b(3'b101), .eq(comparator_20_eq));  // open: gt, lt
  Comparator #(.width(7)) comparator_21 (
    .a(Instruction[31:25]), .b(7'b0000010), .eq(comparator_21_eq));  // open: gt, lt
  Priority_Encoder #(.select(5)) priority_encoder_1 (
    .in0(add), .in1(mul), .in2(sub), .in3(slll), .in4(mulh), .in5(mulhu), .in6(slt), .in7(xorr), .in8(srll),
    .in9(sraa), .in10(orr), .in11(andd), .in12(lb), .in13(lh), .in14(lw), .in15(addi), .in16(slli),
    .in17(slti), .in18(xori), .in19(srli), .in20(srai), .in21(ori), .in22(andi), .in23(sb), .in24(sh),
    .in25(sw), .in26(beq), .in27(bne), .in28(blt), .in29(bge), .in30(bltu), .in31(bgeu), .out(RomInput1));  // open: gs, en_out, en_in
  Comparator #(.width(3)) comparator_22 (.a(Instruction[14:12]), .b(3'b110), .eq(comparator_22_eq));  // open: gt, lt
  Comparator #(.width(3)) comparator_23 (.a(Instruction[14:12]), .b(3'b111), .eq(comparator_23_eq));  // open: gt, lt
  and and_8 (and_8_out, comparator_10_eq, comparator_11_eq);
  and and_9 (and_9_out, comparator_10_eq, comparator_15_eq);
  and and_10 (mulhu, comparator_10_eq, comparator_17_eq);
  and and_11 (slt, comparator_10_eq, comparator_18_eq);
  and and_12 (xorr, comparator_10_eq, comparator_19_eq);
  and and_13 (and_13_out, comparator_10_eq, comparator_20_eq);
  and and_14 (orr, comparator_10_eq, comparator_22_eq);
  and and_15 (andd, comparator_10_eq, comparator_23_eq);
  Comparator #(.width(7)) comparator_24 (.a(Instruction[6:0]), .b(7'b1100011), .eq(comparator_24_eq));  // open: gt, lt
  Comparator #(.width(3)) comparator_25 (.a(Instruction[14:12]), .b(3'b000), .eq(comparator_25_eq));  // open: gt, lt
  Comparator #(.width(7)) comparator_26 (.a(Instruction[6:0]), .b(7'b1100011), .eq(comparator_26_eq));  // open: gt, lt
  not not_1 (not_1_out, BrEq);
  Comparator #(.width(3)) comparator_27 (.a(Instruction[14:12]), .b(3'b001), .eq(comparator_27_eq));  // open: gt, lt
  Demultiplexer #(.enable("false")) demultiplexer_2 (.out0(slll), .out1(mulh), .in(and_9_out), .sel(comparator_16_eq));
  Demultiplexer #(.enable("false")) demultiplexer_3 (.out0(srll), .out1(sraa), .in(and_13_out), .sel(comparator_21_eq));
  and and_16 (is_beq, comparator_24_eq, BrEq, comparator_25_eq);
  and and_17 (is_bne, comparator_26_eq, not_1_out, comparator_27_eq);
  and and_18 (add, and_8_out, comparator_12_eq);
  and and_19 (mul, and_8_out, comparator_13_eq);
  and and_20 (sub, and_8_out, comparator_14_eq);
  Comparator #(.width(7)) comparator_28 (.a(Instruction[6:0]), .b(7'b1100011), .eq(comparator_28_eq));  // open: gt, lt
  Comparator #(.width(3)) comparator_29 (.a(Instruction[14:12]), .b(3'b100), .eq(comparator_29_eq));  // open: gt, lt
  Comparator #(.width(7)) comparator_30 (.a(Instruction[6:0]), .b(7'b1100011), .eq(comparator_30_eq));  // open: gt, lt
  Comparator #(.width(3)) comparator_31 (.a(Instruction[14:12]), .b(3'b101), .eq(comparator_31_eq));  // open: gt, lt
  Priority_Encoder #(.select(2)) priority_encoder_2 (
    .in0(auipc), .in1(lui), .in2(jal), .in3(jalr), .out(RomInput2));  // open: gs, en_out, en_in
  not not_2 (not_2_out, BrLt);
  Comparator #(.width(7)) comparator_32 (.a(Instruction[6:0]), .b(7'b1100011), .eq(comparator_32_eq));  // open: gt, lt
  Comparator #(.width(3)) comparator_33 (.a(Instruction[14:12]), .b(3'b000), .eq(comparator_33_eq));  // open: gt, lt
  Comparator #(.width(3)) comparator_34 (.a(Instruction[14:12]), .b(3'b001), .eq(comparator_34_eq));  // open: gt, lt
  Comparator #(.width(3)) comparator_35 (.a(Instruction[14:12]), .b(3'b100), .eq(comparator_35_eq));  // open: gt, lt
  Comparator #(.width(3)) comparator_36 (.a(Instruction[14:12]), .b(3'b101), .eq(comparator_36_eq));  // open: gt, lt
  Comparator #(.width(3)) comparator_37 (.a(Instruction[14:12]), .b(3'b110), .eq(comparator_37_eq));  // open: gt, lt
  Comparator #(.width(3)) comparator_38 (.a(Instruction[14:12]), .b(3'b111), .eq(comparator_38_eq));  // open: gt, lt
  and and_21 (is_blt, comparator_28_eq, BrLt, comparator_29_eq);
  and and_22 (is_bge, comparator_30_eq, not_2_out, comparator_31_eq);
  and and_23 (beq, comparator_32_eq, comparator_33_eq);
  and and_24 (bne, comparator_32_eq, comparator_34_eq);
  and and_25 (blt, comparator_32_eq, comparator_35_eq);
  and and_26 (bge, comparator_32_eq, comparator_36_eq);
  and and_27 (bltu, comparator_32_eq, comparator_37_eq);
  and and_28 (bgeu, comparator_32_eq, comparator_38_eq);
  Comparator #(.width(7)) comparator_39 (.a(Instruction[6:0]), .b(7'b1100011), .eq(comparator_39_eq));  // open: gt, lt
  Comparator #(.width(3)) comparator_40 (.a(Instruction[14:12]), .b(3'b110), .eq(comparator_40_eq));  // open: gt, lt
  Comparator #(.width(7)) comparator_41 (.a(Instruction[6:0]), .b(7'b1100011), .eq(comparator_41_eq));  // open: gt, lt
  Comparator #(.width(3)) comparator_42 (.a(Instruction[14:12]), .b(3'b111), .eq(comparator_42_eq));  // open: gt, lt
  not not_3 (not_3_out, BrLt);
  and and_29 (is_bltu, comparator_39_eq, BrLt, comparator_40_eq);
  and and_30 (is_bgeu, comparator_41_eq, not_3_out, comparator_42_eq);
  Comparator #(.width(7)) comparator_43 (.a(Instruction[6:0]), .b(7'b0000011), .eq(comparator_43_eq));  // open: gt, lt
  Comparator #(.width(3)) comparator_44 (.a(Instruction[14:12]), .b(3'b000), .eq(comparator_44_eq));  // open: gt, lt
  Comparator #(.width(3)) comparator_45 (.a(Instruction[14:12]), .b(3'b001), .eq(comparator_45_eq));  // open: gt, lt
  Comparator #(.width(3)) comparator_46 (.a(Instruction[14:12]), .b(3'b010), .eq(comparator_46_eq));  // open: gt, lt
  Comparator #(.width(7)) comparator_47 (.a(Instruction[6:0]), .b(7'b0100011), .eq(comparator_47_eq));  // open: gt, lt
  Comparator #(.width(3)) comparator_48 (.a(Instruction[14:12]), .b(3'b000), .eq(comparator_48_eq));  // open: gt, lt
  Comparator #(.width(3)) comparator_49 (.a(Instruction[14:12]), .b(3'b001), .eq(comparator_49_eq));  // open: gt, lt
  Comparator #(.width(3)) comparator_50 (.a(Instruction[14:12]), .b(3'b010), .eq(comparator_50_eq));  // open: gt, lt
  and and_31 (lb, comparator_43_eq, comparator_44_eq);
  and and_32 (lh, comparator_43_eq, comparator_45_eq);
  and and_33 (lw, comparator_43_eq, comparator_46_eq);
  and and_34 (sb, comparator_47_eq, comparator_48_eq);
  and and_35 (sh, comparator_47_eq, comparator_49_eq);
  and and_36 (sw, comparator_47_eq, comparator_50_eq);
  or or_1 (PCSel, jal, is_beq, is_bne, is_blt, is_bge, is_bltu, is_bgeu, jalr);
  Comparator #(.width(7)) comparator_51 (.a(Instruction[6:0]), .b(7'b1101111), .eq(comparator_51_eq));  // open: gt, lt
  Comparator #(.width(7)) comparator_52 (.a(Instruction[6:0]), .b(7'b1100111), .eq(comparator_52_eq));  // open: gt, lt
  Comparator #(.width(3)) comparator_53 (.a(Instruction[14:12]), .b(3'b000), .eq(comparator_53_eq));  // open: gt, lt
  Comparator #(.width(7)) comparator_54 (.a(Instruction[6:0]), .b(7'b0010111), .eq(comparator_54_eq));  // open: gt, lt
  Comparator #(.width(7)) comparator_55 (.a(Instruction[6:0]), .b(7'b0110111), .eq(comparator_55_eq));  // open: gt, lt
  and and_37 (auipc, comparator_54_eq, 1'b1);
  and and_38 (lui, comparator_55_eq, 1'b1);
  and and_39 (jal, comparator_51_eq, 1'b1);
  and and_40 (jalr, comparator_52_eq, comparator_53_eq);
  or or_2 (InputSel, auipc, lui, jal, jalr);

  // Other names for the same wires on the sheet: Opcode[6:0] = Instruction[6:0]; Funct3[2:0] = Instruction[14:12];
  //   Funct7[6:0] = Instruction[31:25]

  // Notes on the sheet:
  //   INPUTS to your circuit
  //   contents of rom_1 (hex, n*v repeats v):
  //   1001 1401 1601 1081 1481 1581 1101 1201 1281 1681 1301 1381 41 41 41 1041 10c1 1141 1241 12c1 16c1
  //   1341 13c1 842 842 842 4*64 74 74 1067 17c7 2069 2041
  //   ROM FOR CONTROL LOGIC
  //   DON'T CHANGE THE LOCATIONS OF THE INPUTS AND OUTPUTS!
  //   This is only if you choose to do the ROM option
  //   OUTPUT from your circuit
  //   Reminder: If using ROM, use combinational logic for PCSel
endmodule
