// Logisim project partial-load.circ as structural Verilog: 1 circuit, main circuit partial_load
module partial_load (
  input  [31:0] Instruction,
  input  [31:0] MemAddress,
  input  [31:0] DataFromMem,
  output [31:0] DataToReg
);

  wire and_1_out, and_6_out, and_10_out, comparator_1_eq, comparator_2_eq, comparator_3_eq, comparator_4_eq,
       comparator_5_eq, comparator_6_eq, comparator_7_eq, comparator_8_eq, comparator_9_eq, comparator_10_eq,
       comparator_11_eq, comparator_12_eq, comparator_13_eq, comparator_14_eq, Data0, Data1, Data2, Data3,
       Data4, Data5, Data6, Data7;
  wire [2:0] DataSel;
  wire [7:0] multiplexer_2_out;
  wire [15:0] multiplexer_3_out;

  Priority_Encoder priority_encoder_1 (
    .in0(Data0), .in1(Data1), .in2(Data2), .in3(Data3), .in4(Data4), .in5(Data5), .in6(Data6), .in7(Data7),
    .out(DataSel));  // open: en_in, gs, en_out
  Comparator #(.width(7)) comparator_1 (.a(Instruction[6:0]), .b(7'b0000011), .eq(comparator_1_eq));  // open: gt, lt
  Comparator #(.width(3)) comparator_2 (.a(Instruction[14:12]), .b(3'b000), .eq(comparator_2_eq));  // open: gt, lt
  and and_1 (and_1_out, comparator_1_eq, comparator_2_eq);
  Comparator #(.width(2)) comparator_3 (.a(MemAddress[1:0]), .b(2'b00), .eq(comparator_3_eq));  // open: gt, lt
  Comparator #(.width(2)) comparator_4 (.a(MemAddress[1:0]), .b(2'b01), .eq(comparator_4_eq));  // open: gt, lt
  Comparator #(.width(2)) comparator_5 (.a(MemAddress[1:0]), .b(2'b10), .eq(comparator_5_eq));  // open: gt, lt
  Comparator #(.width(2)) comparator_6 (.a(MemAddress[1:0]), .b(2'b11), .eq(comparator_6_eq));  // open: gt, lt
  and and_2 (Data0, and_1_out, comparator_3_eq);
  Multiplexer #(.enable("false"), .select(3), .width(32)) multiplexer_1 (
    .in7(DataFromMem), .out(DataToReg), .sel(DataSel));  // open: in0, in1, in2, in3, in4, in5, in6
  and and_3 (Data1, and_1_out, comparator_4_eq);
  and and_4 (Data2, and_1_out, comparator_5_eq);
  and and_5 (Data3, and_1_out, comparator_6_eq);
  Multiplexer #(.enable("false"), .select(3), .width(8)) multiplexer_2 (
    .in0(DataFromMem[7:0]), .in1(DataFromMem[15:8]), .in2(DataFromMem[23:16]), .in3(DataFromMem[31:24]),
    .out(multiplexer_2_out), .sel(DataSel));  // open: in4, in5, in6, in7
  Multiplexer #(.enable("false"), .select(3), .width(16)) multiplexer_3 (
    .in4(DataFromMem[15:0]), .in5(DataFromMem[23:8]), .in6(DataFromMem[31:16]), .out(multiplexer_3_out),
    .sel(DataSel));  // open: in0, in1, in2, in3, in7
  assign DataToReg = {{24{multiplexer_2_out[7]}}, multiplexer_2_out};  // Bit_Extender bit_extender_1
  assign DataToReg = {{16{multiplexer_3_out[15]}}, multiplexer_3_out};  // Bit_Extender bit_extender_2
  Comparator #(.width(7)) comparator_7 (.a(Instruction[6:0]), .b(7'b0000011), .eq(comparator_7_eq));  // open: gt, lt
  Comparator #(.width(3)) comparator_8 (.a(Instruction[14:12]), .b(3'b001), .eq(comparator_8_eq));  // open: gt, lt
  and and_6 (and_6_out, comparator_7_eq, comparator_8_eq);
  Comparator #(.width(2)) comparator_9 (.a(MemAddress[1:0]), .b(2'b00), .eq(comparator_9_eq));  // open: gt, lt
  Comparator #(.width(2)) comparator_10 (.a(MemAddress[1:0]), .b(2'b01), .eq(comparator_10_eq));  // open: gt, lt
  Comparator #(.width(2)) comparator_11 (.a(MemAddress[1:0]), .b(2'b10), .eq(comparator_11_eq));  // open: gt, lt
  and and_7 (Data4, and_6_out, comparator_9_eq);
  and and_8 (Data5, and_6_out, comparator_10_eq);
  and and_9 (Data6, and_6_out, comparator_11_eq);
  Comparator #(.width(7)) comparator_12 (.a(Instruction[6:0]), .b(7'b0000011), .eq(comparator_12_eq));  // open: gt, lt
  Comparator #(.width(3)) comparator_13 (.a(Instruction[14:12]), .b(3'b010), .eq(comparator_13_eq));  // open: gt, lt
  and and_10 (and_10_out, comparator_12_eq, comparator_13_eq);
  Comparator #(.width(2)) comparator_14 (.a(MemAddress[1:0]), .b(2'b00), .eq(comparator_14_eq));  // open: gt, lt
  and and_11 (Data7, and_10_out, comparator_14_eq);

  // Other names for the same wires on the sheet: Opcode[6:0] = Instruction[6:0]; Funct3[2:0] = Instruction[14:12]

  // Notes on the sheet:
  //   INPUTS to your circuit
  //   DON'T CHANGE THE LOCATIONS OF THE INPUTS AND OUTPUTS!
  //   OUTPUT from your circuit
endmodule
