// Logisim project partial-store.circ as structural Verilog: 1 circuit, main circuit partial_store
module partial_store (
  input  [31:0] Instruction,
  input  [31:0] MemAddress,
  input  [31:0] DataFromReg,
  input  MemWEn,
  output [3:0] MemWriteMask,
  output [31:0] DataToMem
);

  wire and_1_out, and_6_out, and_7_out, comparator_2_eq, comparator_3_eq, comparator_4_eq, comparator_5_eq,
       comparator_6_eq, comparator_7_eq, comparator_8_eq, comparator_9_eq, comparator_10_eq,
       comparator_11_eq, comparator_12_eq, comparator_13_eq, comparator_14_eq, not_1_out, Read, sb0, sb1,
       sb2, sb3, Sel1, sh0, sh1, sw;
  wire [1:0] Sel0;
  wire [7:0] Data0, demultiplexer_1_out1;
  wire [15:0] Data4;
  wire [23:16] Data2;
  wire [31:0] Data1;
  wire [31:16] Data5;
  wire [31:24] Data3;

  not not_1 (not_1_out, MemWEn);
  Comparator #(.width(1)) comparator_1 (.a(1'b1), .b(not_1_out), .eq(Read));  // open: gt, lt
  Multiplexer #(.enable("false"), .width(32)) multiplexer_1 (
    .in1({32{1'b0}}), .out(DataToMem), .sel(Read));  // open: in0
  Multiplexer #(.enable("false"), .width(4)) multiplexer_2 (
    .in1(4'b0000), .out(MemWriteMask), .sel(Read));  // open: in0
  Priority_Encoder #(.select(2)) priority_encoder_1 (
    .in0(sb0), .in1(sb1), .in2(sb2), .in3(sb3), .out(Sel0));  // open: gs, en_out, en_in
  Priority_Encoder #(.select(1)) priority_encoder_2 (.in0(sh0), .in1(sh1), .out(Sel1));  // open: gs, en_out, en_in
  Multiplexer #(.enable("false"), .width(32)) multiplexer_3 (
    .in1(DataFromReg), .out(DataToMem), .sel(sw));  // open: in0
  Comparator #(.width(7)) comparator_2 (.a(Instruction[6:0]), .b(7'b0100011), .eq(comparator_2_eq));  // open: gt, lt
  Comparator #(.width(3)) comparator_3 (.a(Instruction[14:12]), .b(3'b000), .eq(comparator_3_eq));  // open: gt, lt
  Demultiplexer #(.enable("false"), .select(2), .width(8)) demultiplexer_1 (
    .out0(Data0), .out1(demultiplexer_1_out1), .out2(Data2), .out3(Data3), .in(DataFromReg[7:0]), .sel(Sel0));
  Demultiplexer #(.enable("false"), .width(16)) demultiplexer_2 (
    .out0(Data4), .out1(Data5), .in(DataFromReg[15:0]), .sel(Sel1));
  and and_1 (and_1_out, comparator_2_eq, MemWEn, comparator_3_eq);
  Comparator #(.width(2)) comparator_4 (.a(MemAddress[1:0]), .b(2'b00), .eq(comparator_4_eq));  // open: gt, lt
  Comparator #(.width(2)) comparator_5 (.a(MemAddress[1:0]), .b(2'b01), .eq(comparator_5_eq));  // open: gt, lt
  Comparator #(.width(2)) comparator_6 (.a(MemAddress[1:0]), .b(2'b10), .eq(comparator_6_eq));  // open: gt, lt
  Comparator #(.width(2)) comparator_7 (.a(MemAddress[1:0]), .b(2'b11), .eq(comparator_7_eq));  // open: gt, lt
  Multiplexer #(.enable("false"), .width(4)) multiplexer_4 (.in1(4'b1111), .out(MemWriteMask), .sel(sw));  // open: in0
  assign Data1 = {{16{1'b0}}, {demultiplexer_1_out1, {8{1'b0}}}};  // Bit_Extender bit_extender_1
  and and_2 (sb0, and_1_out, comparator_4_eq);
  and and_3 (sb1, and_1_out, comparator_5_eq);
  and and_4 (sb2, and_1_out, comparator_6_eq);
  and and_5 (sb3, and_1_out, comparator_7_eq);
  Comparator #(.width(7)) comparator_8 (.a(Instruction[6:0]), .b(7'b0100011), .eq(comparator_8_eq));  // open: gt, lt
  Comparator #(.width(3)) comparator_9 (.a(Instruction[14:12]), .b(3'b001), .eq(comparator_9_eq));  // open: gt, lt
  Comparator #(.width(7)) comparator_10 (.a(Instruction[6:0]), .b(7'b0100011), .eq(comparator_10_eq));  // open: gt, lt
  Comparator #(.width(3)) comparator_11 (.a(Instruction[14:12]), .b(3'b010), .eq(comparator_11_eq));  // open: gt, lt
  Multiplexer #(.enable("false"), .select(2), .width(4)) multiplexer_5 (
    .in0(4'b0001), .in1(4'b0010), .in2(4'b0100), .in3(4'b1000), .out(MemWriteMask), .sel(Sel0));
  Multiplexer #(.enable("false"), .width(4)) multiplexer_6 (
    .in0(4'b0011), .in1(4'b1100), .out(MemWriteMask), .sel(Sel1));
  and and_6 (and_6_out, comparator_8_eq, MemWEn, comparator_9_eq);
  Comparator #(.width(2)) comparator_12 (.a(MemAddress[1:0]), .b(2'b00), .eq(comparator_12_eq));  // open: gt, lt
  Comparator #(.width(2)) comparator_13 (.a(MemAddress[1:0]), .b(2'b10), .eq(comparator_13_eq));  // open: gt, lt
  and and_7 (and_7_out, comparator_10_eq, MemWEn, comparator_11_eq);
  Comparator #(.width(2)) comparator_14 (.a(MemAddress[1:0]), .b(2'b00), .eq(comparator_14_eq));  // open: gt, lt
  and and_8 (sh0, and_6_out, comparator_12_eq);
  and and_9 (sh1, and_6_out, comparator_13_eq);
  and and_10 (sw, and_7_out, comparator_14_eq);
  Multiplexer #(.enable("false"), .width(32)) multiplexer_7 (
    .in0({{16{1'b0}}, Data4}), .in1({Data5, {16{1'b0}}}), .out(DataToMem), .sel(Sel1));
  Multiplexer #(.enable("false"), .select(2), .width(32)) multiplexer_8 (
    .in0({{24{1'b0}}, Data0}), .in1(Data1), .in2({{8{1'b0}}, Data2, {16{1'b0}}}), .in3({Data3, {24{1'b0}}}),
    .out(DataToMem), .sel(Sel0));

  // Other names for the same wires on the sheet: Opcode[6:0] = Instruction[6:0]; Funct3[2:0] = Instruction[14:12]

  // Notes on the sheet:
  //   INPUTS to your circuit
  //   DON'T CHANGE THE LOCATIONS OF THE INPUTS AND OUTPUTS!
  //   OUTPUT from your circuit
endmodule
